# Fritzing sketch Note-Taker Circuit Diagram (saved by Fritzing 0.9.9b)

parts:
  Raspberry_Pi_Pico_with_UPS_HAT = Raspberry Pi Pico
  LCD_Display = mystery part, 4 pins [chip_label=LCD]

nets:
  N1: Raspberry_Pi_Pico_with_UPS_HAT.pin_6, LCD_Display.pin4
  N2: Raspberry_Pi_Pico_with_UPS_HAT.pin_7, LCD_Display.pin3
  N3: Raspberry_Pi_Pico_with_UPS_HAT.pin_36, LCD_Display.pin1
  N4: Raspberry_Pi_Pico_with_UPS_HAT.pin_38, Raspberry_Pi_Pico_with_UPS_HAT.pin_42, LCD_Display.pin2

custom parts:
  Raspberry Pi Pico: Raspberry Pi Pico. Based around the RP2040 microcontroller the Pico is a low cost microcontroller device bringing Raspberry Pi quality, cost, and easy of use to the microcontroller space. Jan 2021, Split part in to two versions: tht (this one) and SMD. This one will drill holes for a .1 in header in pcb to allow plugging in the module as well as providing pads to solder the module to the top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
